# Fritzing sketch sound-meter-uncompressed (saved by Fritzing 0.9.3b)
circuit board: 8.46667cm x 5.64444cm
breadboards: 1

parts:
  R1 = Resistor [tolerance=±5% resistance=220 package=THT]
  R2 = Resistor [tolerance=±5% resistance=220 package=THT]
  R3 = Resistor [tolerance=±5% resistance=220 package=THT]
  LED1 = LED - 5mm [color="Red (633nm)" package="5 mm [THT]"]
  LED2 = LED - 5mm [color="Yellow (592nm)" package="5 mm [THT]"]
  LED3 = LED - 5mm [color="Green (560nm)" package="5 mm [THT]"]
  Part1 = Breakout Board for Electret Microphone
  Part2 = Arduino Nano (Rev3.0)
  U1 = SN74LS14N [package="DIP14 [THT]"]

nets (from the breadboard view):
  N1: R1.Pin_0, U1.1Y
  N2: R1.Pin_1, LED3.cathode
  N3: R2.Pin_0, U1.2Y
  N4: R2.Pin_1, LED2.cathode
  N5: R3.Pin_0, U1.3Y
  N6: R3.Pin_1, LED1.cathode
  VCC: LED1.anode, LED2.anode, LED3.anode, Part1.VCC, Part2.5V, U1.VCC
  GND: Part1.GND, Part2.GND, U1.GND
  N7: Part1.AUD, Part2.A0
  N8: Part2.D7, U1.3A
  N9: Part2.D8, U1.2A
  N10: Part2.D9, U1.1A
